# Fritzing sketch lolin-frtizing (saved by Fritzing 0.9.6b)
breadboards: 1
stripboards: 1

parts:
  U1 = lolin
  BAT1 = Battery Holders [package=lipo-1100mAh]
  R2 = Resistor [tolerance=±5% resistance=10k package="0805 [SMD]"]
  R3 = Resistor [tolerance=±5% resistance=47k package="0805 [SMD]"]
  R4 = Resistor [tolerance=±5% resistance=47k package="0805 [SMD]"]
  RHT1 = Humidity and Temperature Sensor RHT03
  S1 = SWITCH-MOMENTARY-2 [package=reed_switch_pth]
  R5 = Resistor [tolerance=±5% resistance=4.7k package="0805 [SMD]"]

nets:
  N1: U1.connector0, R2.Pin_0, RHT1.Vcc, S1.1
  N2: U1.connector6, R3.Pin_1, R4.Pin_0
  N3: U1.connector12, R2.Pin_1, RHT1.Data-signal
  N4: U1.connector15, RHT1.GND_2
  N5: U1.connector16, BAT1.+, R4.Pin_1
  N6: U1.connector17, BAT1.-, R3.Pin_0
  N7: U1.connector22, R5.Pin_0
  N8: U1.connector31, R5.Pin_1

notes:
  47K resistors
  I use 186500 battery - 3000 mAh
  Battery monitoring is optional, you can conect batery directly - see reed_setting.py
  4,7 k resisotr
  10k resistor
  DHT22 is otional - see reed_setting.py
